# Fritzing sketch cap (saved by Fritzing 0.9.3b)
breadboards: 1

parts:
  LCD1 = LCD screen
  Componente1 = Arduino Uno (Rev3)
  U1 = 555 Timer [package="DIP8 [THT]"]
  U2 = SN74LS14N [package="DIP14 [THT]"]
  C1 = Ceramic Capacitor [capacitance=100nF package="100 mil [THT, multilayer]"]
  R2 = Resistor [tolerance=±5% resistance=220 package=THT]
  R3 = Resistor [tolerance=±5% resistance=220 package=THT]
  R4 = Resistor [tolerance=±5% resistance=220 package=THT]

nets:
  GND: LCD1.VSS, LCD1.R/W, LCD1.LED-, Componente1.GND, U1.Ground, U2.GND, C1.0, R4.Pin_0
  VDD: LCD1.VDD, LCD1.LED+, Componente1.5V, U1.Reset, U1.Vcc_Supply_Voltage, U2.VCC, R3.Pin_0
  N1: LCD1.V0, R4.Pin_1
  N2: LCD1.RS, Componente1.D2
  N3: LCD1.E, Componente1.D3_PWM
  N4: LCD1.DB4, Componente1.D4
  N5: LCD1.DB5, Componente1.D5_PWM
  N6: LCD1.DB6, Componente1.D6_PWM
  N7: LCD1.DB7, Componente1.D7
  N8: Componente1.D8, U2.6Y
  N9: U1.Trigger, U1.Threshold, C1.1, R2.Pin_1
  N10: U1.Output, U2.6A
  N11: U1.Discharge, R2.Pin_0, R3.Pin_1
